# Fritzing sketch Esquematico (saved by Fritzing 0.8.0b)

parts:
  MCU_A = Arduino Uno (Rev3)
  MCU_B = Arduino Uno (Rev3)
  VCC1 = Battery block 9V
  VCC2 = Battery block 9V

nets:
  N1: MCU_A.GND, VCC1.-
  N2: MCU_A.D0/RX, MCU_B.D1/TX
  N3: MCU_A.D1/TX, MCU_B.D0/RX
  N4: MCU_A.VIN, VCC1.+
  N5: MCU_B.GND, VCC2.-
  N6: MCU_B.VIN, VCC2.+
